# Fritzing sketch ESP32_Wiring (saved by Fritzing 0.9.10b)

parts:
  RHT2 = Humidity and Temperature Sensor RHT03
  J2 = shrouded pin header, 10 pins [form="♂ (shrouded male)"]
  U3 = ESP32-38PinWide [part_number=ESP32-38PinWide]
  R2 = Resistor [tolerance=±5% power=0.25 resistance=10k package=THT]

nets:
  N1: RHT2.Vcc, U3.3.3, R2.Pin_1
  N2: RHT2.Data-signal, U3.GPIO14, R2.Pin_0
  N3: RHT2.GND_2, J2.pin1, U3.GND
  N4: J2.pin3, U3.GPIO16
  N5: J2.pin9, U3.GPIO17

notes:
  [display on top, wheel on right]
  display on top, wheel on right
  Honeywell HR-20 serial-test interface

custom parts:
  ESP32-38PinWide: Generic 38-Pin ESP32 with wide format (only access to one side of pins on a breadboard) based on Stephen Lilley's HiLetgo ESP-WROOM-32 ESP32 ESP-32S Development Board.
